# Fritzing sketch Maciek-fritzing_diagram (saved by Fritzing 0.9.3b)
breadboards: 1

parts:
  Part1 = Arduino Uno (Rev3)
  Part7 = Adafruit PowerRelay Feather Wing [part_number="Adafruit #3191"]
  LED3 = LEDs [package=led10mm]
  Part8 = Lilypad Battery Connect
  USBTTL1 = USB TTL Serial Cable  # not connected
  R1 = Resistor [tolerance=±5% resistance=220 package=THT]
  R2 = PHOTOCELL [package=photocell]

nets:
  N1: Part1.A0, R1.Pin_0, R2.P$2
  N2: Part1.D10_PWM/SS, Part7.RELAY
  GND: Part1.GND, Part7.GND, R1.Pin_1
  5V: Part1.5V, Part7.3.3V, R2.P$1
  N3: Part7.COM, LED3.A
  N4: Part7.NO, Part8.+
  N5: LED3.C, Part8.-

custom parts:
  Adafruit PowerRelay Feather Wing: A Feather board without ambition is a Feather board without FeatherWings! This is the Power Relay FeatherWing. It gives you power to control, and control over power. Put simply, you can now turn on and off lamps, fans, solenoids, and other small appliances that run on up to 250VAC or DC power using any Feather board. Compared to our smaller Relay FeatherWings, this one can handle a beefy 1200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
  LEDs: LEDs Standard schematic elements and footprints for 5mm, 3mm, 1206, and 0603 sized LEDs. 5mm - Spark Fun Electronics SKU : COM-00529 (and others)
